// Logisim project assignment4.circ as structural Verilog: 2 circuits, main circuit NAND as Universal Gate
module NAND_as_Universal_Gate (
  input  in_1,
  input  in_2,
  input  in_3,
  input  in_4,
  input  in_5,
  output out_6,
  output out_7,
  output out_8
);

  wire nand_2_out, nand_3_out, nand_4_out;

  nand nand_1 (out_6, in_1, in_1);
  nand nand_2 (nand_2_out, in_2, in_2);
  nand nand_3 (nand_3_out, in_3, in_3);
  nand nand_4 (nand_4_out, in_4, in_5);
  nand nand_5 (out_8, nand_4_out, nand_4_out);
  nand nand_6 (out_7, nand_2_out, nand_3_out);
endmodule

module Basic_Gates (
  input  in_1,
  input  in_2,
  input  in_3,
  input  in_4,
  input  in_5,
  input  in_6,
  input  in_7,
  input  in_8,
  input  in_9,
  input  in_10,
  input  in_11,
  output out_12,
  output out_13,
  output out_14,
  output out_15,
  output out_16
);

  and and_1 (out_12, in_1, in_3);
  and and_2 (out_14, in_5, in_7, in_9);
  not not_1 (out_16, in_11);
  or or_1 (out_13, in_2, in_4);
  or or_2 (out_15, in_6, in_8, in_10);
endmodule
